// Logisim project FPA.circ as structural Verilog: 1 circuit, main circuit main
module main (
  input  [31:0] A,
  input  [31:0] B,
  output out_3,
  output Cout,
  output [10:0] out_5,
  output [19:0] out_6
);

  wire input_1_larger_s_sign, input_1_smaller_s_sign;
  wire [10:0] input_1_larger_exponent, normalizer_1_normalized_exponent;
  wire [31:0] input_1_larger_s_fraction, input_1_shifted_smaller_s_fraction, main_1_p6,
       normalizer_1_normalized_significand, normalizer_2_normalized_significand,
       rounder_1_rounded_significand;

  Input input_1 (
    .A(A), .B(B), .Larger_s_Fraction(input_1_larger_s_fraction), .Larger_s_Sign(input_1_larger_s_sign),
    .Larger_Exponent(input_1_larger_exponent),
    .Shifted_Smaller_s_Fraction(input_1_shifted_smaller_s_fraction), .Smaller_s_sign(input_1_smaller_s_sign));  // open: Exponent_Difference, Smaller_s_Fraction
  // adder32bit_main main_1: pin names not known; wires that end beside it: input_1_larger_s_sign, input_1_larger_s_fraction, input_1_shifted_smaller_s_fraction, input_1_smaller_s_sign, Cout, main_1_p6, out_3, main_1_p6
  normalizer normalizer_1 (
    .exponent_input(input_1_larger_exponent), .significand_input({Cout, main_1_p6[31:1]}),
    .normalized_exponent(normalizer_1_normalized_exponent),
    .normalized_Significand(normalizer_1_normalized_significand));
  Rounder rounder_1 (
    .significand(normalizer_1_normalized_significand), .rounded_significand(rounder_1_rounded_significand));
  normalizer normalizer_2 (
    .exponent_input(normalizer_1_normalized_exponent), .significand_input(rounder_1_rounded_significand),
    .normalized_exponent(out_5),
    .normalized_Significand({normalizer_2_normalized_significand[31:30], out_6, normalizer_2_normalized_significand[9:0]}));
endmodule
